# Fritzing sketch Head electronics (saved by Fritzing 0.9.6b)
breadboards: 1

parts:
  NEOPIXEL2 = Neopixel Strip -- Black (60/m) [part_number=1461]
  Mic1 = KY-038
  Part9 = I2C level shifter bidirectional
  LED3 = LED - 3mm [color="Green (555nm)" current=0.030 package="3 mm [THT]"]
  LED4 = LED - 3mm [color="Green (555nm)" current=0.030 package="3 mm [THT]"]
  LED5 = LED - 3mm [color="Green (555nm)" current=0.030 package="3 mm [THT]"]
  LED6 = LED - 3mm [color="Green (555nm)" current=0.030 package="3 mm [THT]"]

nets:
  N1: NEOPIXEL2.+5V, Mic1.pin3, Part9.HV
  N2: NEOPIXEL2.DI, Part9.HV1
  GND: NEOPIXEL2.GND, Mic1.pin2, Part9.GND, LED3.cathode, LED4.cathode, LED5.cathode, LED6.cathode
  N3: Mic1.pin4, Part9.HV2
  N4: Part9.LV4, Part9.LV3
  N5: Part9.HV3, LED4.anode, LED6.anode
  N6: Part9.HV4, LED3.anode, LED5.anode

notes:
  USB card is used to connect a mic and speaker to the Pi
  [0.5m]
  [0.3m]

custom parts:
  Neopixel Strip -- Black (60/m): Neopixel Strip, Black, 60 pixels per meter.
  KY-038: ky-038 Microphone sound sensor module
